# Fritzing sketch midiIn (saved by Fritzing 0.9.4)

parts:
  DIN1 = DIN-5 jack (MIDI) [package=THT]
  D1 = Diode [package=diode-1n4001]
  R1 = Resistor [tolerance=±5% resistance=220 package="1206 [SMD]"]
  U1 = OPTO_DARL_6N138S [package=8-smd]
  R2 = 330Ω Resistor [package="1206 [SMD]"]
  R3 = 10KΩ Resistor [package="1206 [SMD]"]

nets:
  N1: DIN1.5, D1.A, U1.C
  N2: DIN1.4, R1.Pin_1
  N3: D1.C, R1.Pin_0, U1.A
  GND: U1.GND, R3.Pin_1
  UART 31,250 baud: U1.VB, R2.Pin_1
  5V: U1.VCC, R2.Pin_0
  N4: U1.V0, R3.Pin_0

notes:
  6N138

custom parts:
  OPTO_DARL_6N138S: Optoisolator, darlington pair output
  330Ω Resistor: A generic resistor
  10KΩ Resistor: A generic resistor
